// Digital circuit Célula Memória.dig as structural Verilog
module \Célula_Memória  (
  input  CLK,
  input  E1,
  input  E2,
  input  EN,
  input  CLEAR,
  input  E3,
  input  E4,
  input  E5,
  input  E6,
  input  E7,
  input  E8
);

  wire and_1_out, and_2_out, and_3_out, and_4_out, and_5_out, and_6_out, and_7_out, and_8_out, not_1_out,
       undriven, undriven_2, undriven_3, undriven_4, undriven_5, undriven_6, undriven_7, undriven_8;

  not not_1 (not_1_out, CLEAR);
  flip_flop_D flip_flop_d_1 (.CL(CLK), .D(E1), .En(EN));
  and and_1 (and_1_out, undriven, not_1_out);
  flip_flop_D flip_flop_d_2 (.CL(CLK), .D(E2), .En(EN));
  LED S1 (.in(and_1_out));
  flip_flop_D flip_flop_d_3 (.CL(CLK), .D(E3), .En(EN));
  and and_2 (and_2_out, undriven_2, not_1_out);
  LED S2 (.in(and_2_out));
  flip_flop_D flip_flop_d_4 (.CL(CLK), .D(E4), .En(EN));
  and and_3 (and_3_out, undriven_3, not_1_out);
  LED S3 (.in(and_3_out));
  flip_flop_D flip_flop_d_5 (.CL(CLK), .D(E5), .En(EN));
  and and_4 (and_4_out, undriven_4, not_1_out);
  LED S4 (.in(and_4_out));
  flip_flop_D flip_flop_d_6 (.CL(CLK), .D(E6), .En(EN));
  and and_5 (and_5_out, undriven_5, not_1_out);
  LED S5 (.in(and_5_out));
  and and_6 (and_6_out, undriven_6, not_1_out);
  flip_flop_D flip_flop_d_7 (.CL(CLK), .D(E7), .En(EN));
  LED S6 (.in(and_6_out));
  and and_7 (and_7_out, undriven_7, not_1_out);
  flip_flop_D flip_flop_d_8 (.CL(CLK), .D(E8), .En(EN));
  LED S7 (.in(and_7_out));
  and and_8 (and_8_out, undriven_8, not_1_out);
  LED S8 (.in(and_8_out));
endmodule
