// Digital circuit Flip-Flop-EscravoMestre.dig as structural Verilog
module Flip_Flop_EscravoMestre (
  input  J,
  input  CLK,
  input  K,
  input  Preset,
  input  Clr,
  output out_6,
  output out_7
);

  wire nand_1_out, nand_2_out, nand_3_out, nand_4_out, nand_5_out, nand_6_out, not_1_out;

  nand nand_1 (nand_1_out, CLK, CLK, out_6);
  nand nand_2 (nand_2_out, K, CLK, out_7);
  not not_1 (not_1_out, CLK);
  nand nand_3 (nand_3_out, nand_2_out, Clr, nand_4_out);
  nand nand_4 (nand_4_out, nand_1_out, Preset, nand_3_out);
  nand nand_5 (nand_5_out, nand_3_out, not_1_out);
  nand nand_6 (nand_6_out, nand_4_out, not_1_out);
  nand nand_7 (out_6, nand_5_out, out_7);
  nand nand_8 (out_7, nand_6_out, Preset, out_6);

  assign J = CLK;
endmodule
