// Digital circuit Flip-Flop-JK.dig as structural Verilog
module Flip_Flop_JK (
  input  J,
  input  K,
  input  Clk,
  output O,
  output O_2
);

  wire and_1_out, and_2_out;

  and and_1 (and_1_out, O, J, Clk);
  and and_2 (and_2_out, Clk, K, O_2);
  nor nor_1 (O, and_1_out, O_2);
  nor nor_2 (O_2, O, and_2_out);
endmodule
