// Digital circuit ULA.dig as structural Verilog
module ULA (
);

  Somador_Completo somador_completo_1 ();  // open: E1, E2, Cin, SUM, CARRY
  Somador_Completo somador_completo_2 ();  // open: E1, E2, Cin, SUM, CARRY
endmodule
