// Digital circuit flip-flop-D.dig as structural Verilog
module flip_flop_D (
  input  CLK,
  input  D,
  input  EN,
  output O,
  output O_2
);

  wire nand_1_out, nand_2_out, not_1_out;

  not not_1 (not_1_out, D);
  nand nand_1 (nand_1_out, D, EN, CLK);
  nand nand_2 (nand_2_out, CLK, EN, not_1_out);
  nand nand_3 (O, nand_1_out, O_2);
  nand nand_4 (O_2, O, nand_2_out);
endmodule
